# Fritzing sketch ADSR wave gen AREF test (saved by Fritzing 0.9.3b)
breadboards: 1

parts:
  Part2 = Adafruit Feather M0 Express [part_number="Adafruit #3403"]
  TRS1 = Audio Jack (TRS) 3.5mm [package="4Ucon 08780 [THT]"]

nets:
  N1: Part2.GND, TRS1.Sleeve
  N2: Part2.A0, TRS1.Tip

notes:
  AD9833 Feather Wing
  A0 DAC out to TRS jack (audio out)
  wave gen out to DAC AREF

custom parts:
  Adafruit Feather M0 Express: We love all our Feathers equally, but this Feather is very special. It's our first Feather that is specifically designed for use with CircuitPython! CircuitPython is our beginner-oriented flavor of MicroPython - and as the name hints at, its a small but full-featured version of the popular Python programming language specifically for use with circuitry and electronics. That doesn't mean you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
