# Fritzing sketch DAC AREF volume control (saved by Fritzing 0.9.3b)
breadboards: 1

parts:
  Part2 = Adafruit Feather M0 Express [part_number="Adafruit #3403"]
  TRS1 = Audio Jack (TRS) 3.5mm [package="4Ucon 08780 [THT]"]
  R1 = Rotary Potentiometer (Large) [maximum_resistance=100kΩ package=THT]
  R2 = Resistor [tolerance=±5% resistance=2k package="0402 [SMD]"]

nets:
  N1: Part2.GND, TRS1.Sleeve, R2.Pin_1
  N2: Part2.A1, TRS1.Ring
  N3: Part2.A0, TRS1.Tip
  N4: Part2.AREF, R1.wiper
  N5: Part2.+3V3, R1.leg2
  N6: R1.leg1, R2.Pin_0

notes:
  A0 DAC out to TRS jack (audio out)
  cut the AREF --> 3v3 trace
  10K potentiometer + 2K resistor

custom parts:
  Adafruit Feather M0 Express: We love all our Feathers equally, but this Feather is very special. It's our first Feather that is specifically designed for use with CircuitPython! CircuitPython is our beginner-oriented flavor of MicroPython - and as the name hints at, its a small but full-featured version of the popular Python programming language specifically for use with circuitry and electronics. That doesn't mean you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
